# Fritzing sketch Analog_Mux_TC74HC4051 (saved by Fritzing 0.9.10b)
breadboards: 1

parts:
  Mod1 = Amica NodeMCU DEVKIT 1.0
  MUX1 = 74HC4051 [package="DIP (Dual Inline) [THT]"]
  R2 = Resistor [tolerance=±5% resistance=10000 package="2010 [SMD]"]
  R3 = PHOTOCELL [package=photocell]
  R4 = TRIMPOT [maximum_resistance=10kΩ knob_status=50% power=0.5W package=3362u-2]

nets:
  N1: Mod1.pin1, Mod1.pin_10, Mod1.pin_26, MUX1.VDD, R2.Pin_0, R4.CW
  N2: Mod1.pin2, Mod1.pin_9, Mod1.pin_25, Mod1.pin_29, MUX1.INH, MUX1.VEE, MUX1.VSS, R3.P$1, R4.CCW
  N3: Mod1.pin_13, MUX1.A
  N4: Mod1.pin_14, MUX1.B
  N5: Mod1.pin_15, MUX1.C
  N6: Mod1.pin_16, MUX1.IO
  N7: MUX1.IO0, R2.Pin_1, R3.P$2, R4.WIPER

custom parts:
  74HC4051: 8 channel analog multiplexer/demultiplexer
